# Fritzing sketch lab_1 (saved by Fritzing 0.9.2b)
breadboards: 1

parts:
  Part1 = Arduino Uno (Rev3)
  R1 = Resistor [tolerance=±5% resistance=560 package=THT]
  R2 = Resistor [tolerance=±5% resistance=560 package=THT]
  S1 = Pushbutton [package="[THT]"]
  R3 = Resistor [tolerance=±5% resistance=560 package=THT]
  LED2 = LED - 5mm [color="Red (633nm)" package="5 mm [THT]"]
  LED3 = LED - 5mm [color="Red (633nm)" package="5 mm [THT]"]

nets:
  N1: Part1.D3_PWM, Part1.5V, S1.Pin_3, S1.Pin_4, R3.Pin_0, R3.Pin_1
  N2: Part1.D4, LED3.cathode
  N3: Part1.D5_PWM, LED2.cathode
  N4: R1.Pin_0, LED2.anode
  N5: R1.Pin_1, R2.Pin_1
  N6: R2.Pin_0, LED3.anode
  N7: S1.Pin_1, S1.Pin_2
