# Fritzing sketch lab_7 (saved by Fritzing 0.8.7b)
breadboards: 1

parts:
  Part1 = Arduino Uno (Rev3)
  LED5 = RGB LED (com. anode, rbg) [package="5 mm [THT]"]
  R12 = Resistor [tolerance=±5% resistance=560 package=THT]
  R13 = Resistor [tolerance=±5% resistance=560 package=THT]
  R14 = Resistor [tolerance=±5% resistance=560 package=THT]
  U1 = TMP36 [package=to-92-kit]

nets:
  N1: Part1.A1, U1.VOUT
  N2: Part1.D8, R12.Pin_0
  N3: Part1.D6_PWM, R14.Pin_0
  N4: Part1.D7, R13.Pin_0
  5V: Part1.5V, LED5.common_anode, U1.VCC
  GND: Part1.GND, U1.GND
  N5: LED5.red_cathode, R12.Pin_1
  N6: LED5.blue_cathode, R13.Pin_1
  N7: LED5.green_cathode, R14.Pin_1
